# Fritzing sketch smart-iot-drop-off-pick-up-parcel (saved by Fritzing 0.9.3b)

parts:
  M1 = fc-51 [package=THT]
  S1 = Pushbutton [package="[THT]"]
  R1 = Resistor [tolerance=±5% resistance=10 package=THT]
  M2 = DC Motor
  Power_plug1 = Power plug
  U3 = RELAY [package=relay-g5q]
  Q1 = NPN-Transistor [package="TO92 [THT]"]
  D1 = Rectifier Diode [part_number=1N4001 package="300 mil [THT]"]
  R2 = Resistor [tolerance=±5% resistance=220 package=THT]
  LED1 = LED - 5mm [color="Red (633nm)" package="5 mm [THT]"]
  AMS1 = AMS1777 5V regulator module
  LED2 = LED - 5mm [color="Red (633nm)" package="5 mm [THT]"]
  R3 = Resistor [tolerance=±5% resistance=220 package=THT]
  U2 = ESP 32 DEVKIT DOIT

nets:
  D34: M1.pin1
  GND: M1.pin2, R1.Pin_1, M2.pin_2, Q1.E, R2.Pin_1, LED2.anode, U2.GND
  5V: M1.pin3, S1.Pin_3, S1.Pin_4, U3.COIL1, D1.cathode, LED1.anode, AMS1.VOUT+, U2.Vin
  D14: S1.Pin_2, R1.Pin_0
  N1: M2.pin_1, U3.NO
  N2: Power_plug1.GND, AMS1.GND-_(input)
  12V: Power_plug1.VCC, U3.MAIN, AMS1.VIN+
  N3: U3.COIL2, Q1.C, D1.anode
  D26: Q1.B
  N4: R2.Pin_0, LED2.cathode
  N5: LED1.cathode, R3.Pin_0
  gnd: AMS1.GND-_(output), R3.Pin_1

notes:
  Solenoid lock
  ir sensor
  button
  relay connection
  voltage regulator 5V
  esp32

custom parts:
  AMS1777 5V regulator module: AMS1777 5V regulator module source : https://github.com/ShenTengTu/fritzing_parts/tree/master/voltage%20regulator/AMS1117_5V_regulator_module
